// Logisim project BrainfuckPC_full.circ as structural Verilog
module ADDC (
  input  A,
  input  B,
  input  Cin,
  output Cout,
  output Y
);

  wire and_1_out, and_2_out, xor_1_out;

  and and_1 (and_1_out, A, B);
  xor xor_1 (xor_1_out, A, B);
  and and_2 (and_2_out, xor_1_out, Cin);
  xor xor_2 (Y, xor_1_out, Cin);
  or or_1 (Cout, and_1_out, and_2_out);
endmodule

module ADDC_16bit (
  input  B0,
  input  B1,
  input  B2,
  input  B3,
  input  B4,
  input  B5,
  input  B6,
  input  B7,
  input  B8,
  input  B9,
  input  B10,
  input  B11,
  input  B12,
  input  B13,
  input  B14,
  input  B15,
  input  C_IN,
  output Y0,
  output Y1,
  output Y2,
  output Y3,
  output Y4,
  output Y5,
  output Y6,
  output Y7,
  output Y8,
  output Y9,
  output Y10,
  output Y11,
  output Y12,
  output Y13,
  output Y14,
  output Y15,
  output C_OUT
);

  wire addc_1_cout, addc_2_cout, addc_3_cout, addc_4_cout, addc_5_cout, addc_6_cout, addc_7_cout,
       addc_8_cout, addc_9_cout, addc_10_cout, addc_11_cout, addc_12_cout, addc_13_cout, addc_14_cout,
       addc_15_cout;
  wire [15:0] undriven;

  ADDC addc_1 (.Y(Y0), .Cin(C_IN), .A(undriven[0]), .B(B0), .Cout(addc_1_cout));
  ADDC addc_2 (.Y(Y1), .Cin(addc_1_cout), .A(undriven[1]), .B(B1), .Cout(addc_2_cout));
  ADDC addc_3 (.Y(Y2), .Cin(addc_2_cout), .A(undriven[2]), .B(B2), .Cout(addc_3_cout));
  ADDC addc_4 (.Y(Y3), .Cin(addc_3_cout), .A(undriven[3]), .B(B3), .Cout(addc_4_cout));
  ADDC addc_5 (.Y(Y4), .Cin(addc_4_cout), .A(undriven[4]), .B(B4), .Cout(addc_5_cout));
  ADDC addc_6 (.Y(Y5), .Cin(addc_5_cout), .A(undriven[5]), .B(B5), .Cout(addc_6_cout));
  ADDC addc_7 (.Y(Y6), .Cin(addc_6_cout), .A(undriven[6]), .B(B6), .Cout(addc_7_cout));
  ADDC addc_8 (.Y(Y7), .Cin(addc_7_cout), .A(undriven[7]), .B(B7), .Cout(addc_8_cout));
  ADDC addc_9 (.Y(Y8), .Cin(addc_8_cout), .A(undriven[8]), .B(B8), .Cout(addc_9_cout));
  ADDC addc_10 (.Y(Y9), .Cin(addc_9_cout), .A(undriven[9]), .B(B9), .Cout(addc_10_cout));
  ADDC addc_11 (.Y(Y10), .Cin(addc_10_cout), .A(undriven[10]), .B(B10), .Cout(addc_11_cout));
  ADDC addc_12 (.Y(Y11), .Cin(addc_11_cout), .A(undriven[11]), .B(B11), .Cout(addc_12_cout));
  ADDC addc_13 (.Y(Y12), .Cin(addc_12_cout), .A(undriven[12]), .B(B12), .Cout(addc_13_cout));
  ADDC addc_14 (.Y(Y13), .Cin(addc_13_cout), .A(undriven[13]), .B(B13), .Cout(addc_14_cout));
  ADDC addc_15 (.Y(Y14), .Cin(addc_14_cout), .A(undriven[14]), .B(B14), .Cout(addc_15_cout));
  ADDC addc_16 (.Y(Y15), .Cin(addc_15_cout), .A(undriven[15]), .B(B15), .Cout(C_OUT));
endmodule
